# Fritzing sketch moat-shark (saved by Fritzing 1.0.2b)
circuit board: 4.99999cm x 10cm
breadboards: 2

parts:
  100Kfm2 = Rotary Potentiometer (Small) [maximum_resistance=100kΩ knob_status=50% power=0.5W package=THT]
  4040A = CD4040E [package="DIP16 [THT]"]
  XR2206 = XR2206 [package=dil16]
  100Ks1 = Rotary Potentiometer (Small) [maximum_resistance=100kΩ knob_status=50% power=0.5W package=THT]  # not connected
  j40 = female pin header, 6 pins [form="♀ (female)"]
  4_7k = Resistor [tolerance=±5% resistance=4.7k power=0.25W package=THT]
  Jx1 = female pin header, 2 pins [form="♀ (female)"]
  A/B = female pin header, 2 pins [form="♀ (female)"]
  Jx2 = female pin header, 2 pins [form="♀ (female)"]
  1uf = Electrolytic Capacitor [capacitance=1µF voltage=16V package="100 mil [THT, electrolytic]"]
  4_7k_2 = Resistor [tolerance=±5% resistance=4.7k power=0.25W package=THT]
  68nf = Ceramic Capacitor [capacitance=68nF voltage=16V package="200 mil [THT, multilayer]"]
  220o = Resistor [tolerance=±5% resistance=220 power=0.25W package=THT]
  100Kfm1 = Rotary Potentiometer (Small) [maximum_resistance=100kΩ knob_status=50% power=0.5W package=THT]
  4_7k_3 = Resistor [tolerance=±1% resistance=4.7k power=0.25W package=THT]
  4_7k_4 = Resistor [tolerance=±1% resistance=4.7k power=0.25W package=THT]
  100Kamp = Rotary Potentiometer (Small) [maximum_resistance=100kΩ knob_status=50% power=0.5W package=THT]
  1kshape = Rotary Potentiometer (Small) [maximum_resistance=1kΩ knob_status=50% power=0.5W package=THT]
  4_7k3 = Resistor [tolerance=±5% resistance=4.7k power=0.25W package=THT]
  TRS1 = Audio Jack (TRS) 3.5mm [package="PG203J [THT]"]
  Power_plug1 = Power plug
  out = female pin header, 2 pins [form="♀ (female)"]
  100Ks2 = Rotary Potentiometer (Small) [maximum_resistance=100kΩ knob_status=50% power=0.5W package=THT]
  Jm2 = female pin header, 3 pins [form="♀ (female)"]
  LM324 = LM124-324 Quad Opamp [package="DIP (Dual Inline)"]
  100K = Resistor [tolerance=±5% resistance=100k power=0.25W package=THT]
  1K = Resistor [tolerance=±5% resistance=1k power=0.25W package=THT]
  100K_2 = Resistor [tolerance=±5% resistance=100k power=0.25W package=THT]
  1K_2 = Resistor [tolerance=±5% resistance=1k power=0.25W package=THT]
  100K_3 = Resistor [tolerance=±5% resistance=100k power=0.25W package=THT]
  1K_3 = Resistor [tolerance=±5% resistance=1k power=0.25W package=THT]
  opcom = female pin header, 4 pins [form="♀ (female)"]
  Jamp5 = female pin header, 1 pin [form="♀ (female)"]
  Jamp4 = female pin header, 1 pin [form="♀ (female)"]
  Jamp1 = female pin header, 1 pin [form="♀ (female)"]
  Jamp2 = female pin header, 2 pins [form="♀ (female)"]
  Jamp3 = female pin header, 2 pins [form="♀ (female)"]
  Jamp6 = female pin header, 2 pins [form="♀ (female)"]
  47u = Electrolytic Capacitor [capacitance=47µF voltage=35V package="100 mil [THT, electrolytic]"]
  4_7k4 = Resistor [tolerance=±5% resistance=4.7k power=0.25W package=THT]
  LED3 = LED - 3mm [color="Blue (505nm)" current=0.030A package="3 mm [THT]"]
  j42 = female pin header, 4 pins [form="♀ (female)"]
  1uF = Electrolytic Capacitor [capacitance=1µF voltage=35V package="100 mil [THT, electrolytic]"]
  2N3907 = NPN-Transistor [package="TO92 [THT]"]
  10K = Resistor [tolerance=±5% resistance=10k power=0.25W package=THT]
  1K1 = Resistor [tolerance=±5% resistance=1k power=0.25W package=THT]
  1K2 = Resistor [tolerance=±5% resistance=1k power=0.25W package=THT]
  2N3908 = NPN-Transistor [package="TO92 [THT]"]
  10K_2 = Resistor [tolerance=±5% resistance=10k power=0.25W package=THT]
  1K_4 = Resistor [tolerance=±5% resistance=1k power=0.25W package=THT]
  1K_5 = Resistor [tolerance=±5% resistance=1k power=0.25W package=THT]
  LED2 = LED - 3mm [color="Blue (505nm)" current=0.030A package="3 mm [THT]"]
  2N3909 = NPN-Transistor [package="TO92 [THT]"]
  10K_3 = Resistor [tolerance=±5% resistance=10k power=0.25W package=THT]
  1K5 = Resistor [tolerance=±5% resistance=1k power=0.25W package=THT]
  1K_6 = Resistor [tolerance=±5% resistance=1k power=0.25W package=THT]
  LED1 = LED - 3mm [color="Blue (505nm)" current=0.030A package="3 mm [THT]"]
  S10 = SPST Switch [package=switch-spdt_kit]
  47u_2 = Electrolytic Capacitor [capacitance=1µF voltage=35V package="100 mil [THT, electrolytic]"]
  PT2399 = IC, DIP package, 16 pins [chip_label=IC]
  j43 = female pin header, 6 pins [form="♀ (female)"]  # not connected
  47u_3 = Electrolytic Capacitor [capacitance=47µF voltage=35V package="100 mil [THT, electrolytic]"]
  100n = Ceramic Capacitor [capacitance=100nF voltage=16V package="200 mil [THT, multilayer]"]
  100n_2 = Ceramic Capacitor [capacitance=100nF voltage=16V package="200 mil [THT, multilayer]"]
  D1 = Schottky Diode [part_number=1N5817 package="300 mil [THT]"]
  L78L05 = NPN-Transistor [package="TO92 [THT]"]

nets:
  N1: 100Kfm2.leg1, Jx2.pin1, Jx2.pin2, S10.P
  N2: 100Kfm2.wiper, 4_7k.Pin_1
  GND: 100Kfm2.leg2, 4040A.Vss, 4040A.Reset, XR2206.GND, 4_7k_3.Pin_0, 100Kamp.leg1, 1kshape.wiper, TRS1.Sleeve, Power_plug1.GND, out.pin1, LM324.VCC-, 47u.-, LED3.cathode, 2N3907.C, 2N3908.C, LED2.cathode, 2N3909.C, LED1.cathode, 47u_2.-, PT2399.pin3, PT2399.pin4, PT2399.pin10, 47u_3.-, 100n.1, 100n_2.1, L78L05.B
  N3: 4040A.Q13, j40.pin1
  N4: 4040A.Q14, j40.pin2
  N5: 4040A.Q6, j40.pin3
  N6: 4040A.Q5, j40.pin4
  N7: 4040A.Q7, j40.pin5
  N8: 4040A.Q4, j40.pin6
  N9: 4040A.Input_signal, LM324.2OUT, 100K_2.Pin_1, 1K_4.Pin_1
  N10: 4040A.Q9, j42.pin4
  N11: 4040A.Q8, j42.pin3
  N12: 4040A.Q10, j42.pin2
  N13: 4040A.Q11, j42.pin1
  9V: 4040A.Vdd, XR2206.VCC, 4_7k_4.Pin_0, Power_plug1.VCC, LM324.VCC+, 10K.Pin_0, 10K_2.Pin_0, 10K_3.Pin_1, D1.anode
  N14: XR2206.STO, 1uf.-
  N15: XR2206.MO, 4_7k3.Pin_1
  N16: XR2206.TC1, 68nf.0
  N17: XR2206.TC2, 68nf.1
  N18: XR2206.TR1, 4_7k_2.Pin_0
  N19: XR2206.TR2, 4_7k.Pin_0
  N20: XR2206.FSKI, A/B.pin1, A/B.pin2
  N21: XR2206.SYNCO, 47u_2.+
  N22: XR2206.WAVEA1, 220o.Pin_1
  N23: XR2206.WAVEA2, 220o.Pin_0
  N24: XR2206.SYMA1, 1kshape.leg2
  N25: XR2206.SYMA2, 1kshape.leg1
  N26: Jx1.pin1, Jx1.pin2, 100Kfm1.leg1
  N27: 1uf.+, TRS1.Ring, TRS1.Tip, out.pin2
  N28: 4_7k_2.Pin_1, 100Kfm1.wiper
  N29: 4_7k_3.Pin_1, 4_7k_4.Pin_1, 4_7k3.Pin_0
  N30: 100Kamp.leg2, 4_7k4.Pin_0, 1K2.Pin_1
  N31: 100Ks2.leg1, Jm2.pin3
  N32: 100Ks2.wiper, Jm2.pin2
  N33: 100Ks2.leg2, Jm2.pin1
  N34: LM324.1OUT, 100K_3.Pin_0, 1K_6.Pin_1
  N35: LM324.1IN-, Jamp5.pin1
  N36: LM324.1IN+, 100K_3.Pin_1, 1K_3.Pin_0
  N37: LM324.2IN+, 100K_2.Pin_0, 1K_2.Pin_1
  N38: LM324.2IN-, Jamp4.pin1
  N39: LM324.3OUT, 100K.Pin_0, 4_7k4.Pin_1
  N40: LM324.3IN-, Jamp1.pin1
  N41: LM324.3IN+, 100K.Pin_1, 1K.Pin_1
  N42: 1K.Pin_0, Jamp2.pin1, Jamp2.pin2
  N43: 1K_2.Pin_0, Jamp3.pin1, Jamp3.pin2
  N44: 1K_3.Pin_1, Jamp6.pin1, Jamp6.pin2
  N45: opcom.pin1, opcom.pin2, opcom.pin3, opcom.pin4
  N46: 47u.+, PT2399.pin2
  N47: LED3.anode, 1K1.Pin_0
  N48: 1uF.-, S10.S, PT2399.pin8, 100n.0
  N49: 1uF.+, S10.O
  N50: 2N3907.E, 10K.Pin_1, 1K1.Pin_1
  N51: 2N3907.B, 1K2.Pin_0
  N52: 2N3908.E, 10K_2.Pin_1, 1K_5.Pin_1
  N53: 2N3908.B, 1K_4.Pin_0
  N54: 1K_5.Pin_0, LED2.anode
  N55: 2N3909.E, 10K_3.Pin_0, 1K5.Pin_1
  N56: 2N3909.B, 1K_6.Pin_0
  N57: 1K5.Pin_0, LED1.anode
  N58: PT2399.pin1, 47u_3.+, L78L05.E
  N59: PT2399.pin7, 100n_2.0
  N60: D1.cathode, L78L05.C

notes:
  moat
  blueprint@poetaster.de 2024

custom parts:
  CD4040E: CD4020B, CD4024B, and CD4040B are ripple-carry binary counters. All counter stages are master-slave flip-flops. The state of a counter advances one count on the negative transition of each input pulse; a high level on the RESET line resets the counter to its all zeros state. Schmitt trigger action on the input-pulse line permits unlimited rise and fall times. All inputs and outputs are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
