# Fritzing sketch moat (saved by Fritzing 1.0.2b)
circuit board: 5cm x 10cm
breadboards: 2

parts:
  100Kfm2 = Rotary Potentiometer (Small) [maximum_resistance=100kΩ knob_status=50% power=0.5W package=THT]
  4040 = CD4040E [package="DIP16 [THT]"]
  XR2206 = XR2206 [package=dil16]
  100Ks1 = Rotary Potentiometer (Small) [maximum_resistance=100kΩ knob_status=50% power=0.5W package=THT]
  j40 = female pin header, 6 pins [form="♀ (female)"]
  4_7k = Resistor [tolerance=±5% resistance=4.7k power=0.25W package=THT]
  Jx1 = female pin header, 2 pins [form="♀ (female)"]
  JAB = female pin header, 2 pins [form="♀ (female)"]
  Jx2 = female pin header, 2 pins [form="♀ (female)"]
  1uf = Electrolytic Capacitor [capacitance=1µF voltage=16V package="100 mil [THT, electrolytic]"]
  4_7k_2 = Resistor [tolerance=±5% resistance=4.7k power=0.25W package=THT]
  68nf = Ceramic Capacitor [capacitance=68nF voltage=16V package="200 mil [THT, multilayer]"]
  220o = Resistor [tolerance=±5% resistance=220 power=0.25W package=THT]
  Jm1 = female pin header, 3 pins [form="♀ (female)"]
  100Kfm1 = Rotary Potentiometer (Small) [maximum_resistance=100kΩ knob_status=50% power=0.5W package=THT]
  1k = Resistor [tolerance=±1% resistance=1k power=0.25W package=THT]
  1k_2 = Resistor [tolerance=±1% resistance=1k power=0.25W package=THT]
  100Kamp = Rotary Potentiometer (Small) [maximum_resistance=100kΩ knob_status=50% power=0.5W package=THT]
  100 = Resistor [tolerance=±5% resistance=100 power=0.25W package=THT]
  1kshap = Rotary Potentiometer (Small) [maximum_resistance=1kΩ knob_status=50% power=0.5W package=THT]
  4_7k3 = Resistor [tolerance=±5% resistance=4.7k power=0.25W package=THT]
  TRS1 = Audio Jack (TRS) 3.5mm [package="PG203J [THT]"]
  Power_plug1 = Power plug
  out = female pin header, 2 pins [form="♀ (female)"]
  100Ks2 = Rotary Potentiometer (Small) [maximum_resistance=100kΩ knob_status=50% power=0.5W package=THT]
  Jm2 = female pin header, 3 pins [form="♀ (female)"]
  LM324 = LM124-324 Quad Opamp [package="DIP (Dual Inline)"]
  100K = Resistor [tolerance=±5% resistance=100k power=0.25W package=THT]
  1K = Resistor [tolerance=±5% resistance=1k power=0.25W package=THT]
  100K_2 = Resistor [tolerance=±5% resistance=100k power=0.25W package=THT]
  1K_2 = Resistor [tolerance=±5% resistance=1k power=0.25W package=THT]
  100K_3 = Resistor [tolerance=±5% resistance=100k power=0.25W package=THT]
  1K_3 = Resistor [tolerance=±5% resistance=1k power=0.25W package=THT]
  4040_2 = CD4040E [package="DIP16 [THT]"]
  j41 = female pin header, 6 pins [form="♀ (female)"]
  opcom = female pin header, 4 pins [form="♀ (female)"]
  Jamp5 = female pin header, 1 pin [form="♀ (female)"]
  Jamp4 = female pin header, 1 pin [form="♀ (female)"]
  Jamp1 = female pin header, 1 pin [form="♀ (female)"]
  Jamp2 = female pin header, 2 pins [form="♀ (female)"]
  Jamp3 = female pin header, 2 pins [form="♀ (female)"]
  Jamp6 = female pin header, 2 pins [form="♀ (female)"]
  C1 = Electrolytic Capacitor [capacitance=47µF voltage=35V package="100 mil [THT, electrolytic]"]
  4_7k4 = Resistor [tolerance=±5% resistance=4.7k power=0.25W package=THT]
  LED3 = LED - 3mm [color="Blue (505nm)" current=0.030A package="3 mm [THT]"]
  100_2 = Resistor [tolerance=±5% resistance=100 power=0.25W package=THT]
  100_3 = Resistor [tolerance=±5% resistance=100 power=0.25W package=THT]
  LED4 = LED - 3mm [color="Blue (505nm)" current=0.030A package="3 mm [THT]"]
  j42 = female pin header, 4 pins [form="♀ (female)"]
  LED5 = LED - 3mm [color="Blue (505nm)" current=0.030A package="3 mm [THT]"]  # not connected

nets (from the schematic view):
  N1: 100Kfm2.leg1, Jx2.pin1, Jx2.pin2, 100Ks2.wiper, Jm2.pin2
  N2: 100Kfm2.wiper, 4_7k.Pin_1
  GND: 100Kfm2.leg2, 4040.Vss, 4040.Reset, XR2206.GND, 100Kfm1.leg2, 1k.Pin_0, 100Kamp.leg1, 1kshap.wiper, TRS1.Sleeve, Power_plug1.GND, out.pin1, LM324.VCC-, 4040_2.Vss, 4040_2.Reset, C1.-, LED3.cathode, LED4.cathode
  N3: 4040.Q13, j40.pin1
  N4: 4040.Q14, j40.pin2
  N5: 4040.Q6, j40.pin3
  N6: 4040.Q5, j40.pin4
  N7: 4040.Q7, j40.pin5
  N8: 4040.Q4, j40.pin6
  N9: 4040.Q1, 100Ks1.leg2, Jm1.pin1, 100.Pin_1
  N10: 4040.Input_signal, LM324.2OUT, 100K_2.Pin_1
  N11: 4040.Q9, j42.pin4
  N12: 4040.Q8, j42.pin3
  N13: 4040.Q10, j42.pin2
  N14: 4040.Q11, j42.pin1
  9V: 4040.Vdd, XR2206.VCC, 1k_2.Pin_0, Power_plug1.VCC, LM324.VCC+, 4040_2.Vdd
  N15: XR2206.AMSI, 100Kamp.wiper
  N16: XR2206.STO, 1uf.-
  N17: XR2206.MO, 4_7k3.Pin_1
  N18: XR2206.TC1, 68nf.0
  N19: XR2206.TC2, 68nf.1
  N20: XR2206.TR1, 4_7k_2.Pin_0
  N21: XR2206.TR2, 4_7k.Pin_0
  N22: XR2206.FSKI, JAB.pin1, JAB.pin2
  N23: XR2206.WAVEA1, 220o.Pin_1
  N24: XR2206.WAVEA2, 220o.Pin_0
  N25: XR2206.SYMA1, 1kshap.leg2
  N26: XR2206.SYMA2, 1kshap.leg1
  N27: 100Ks1.leg1, Jm1.pin3
  N28: 100Ks1.wiper, Jx1.pin1, Jx1.pin2, Jm1.pin2, 100Kfm1.leg1
  N29: 1uf.+, TRS1.Ring, TRS1.Tip, out.pin2
  N30: 4_7k_2.Pin_1, 100Kfm1.wiper
  N31: 1k.Pin_1, 1k_2.Pin_1, 4_7k3.Pin_0
  N32: 100Kamp.leg2, C1.+, 4_7k4.Pin_0, 100_2.Pin_0
  N33: 100Ks2.leg1, Jm2.pin3
  N34: 100Ks2.leg2, Jm2.pin1, 4040_2.Q1, 100_3.Pin_1
  N35: LM324.1OUT, 100K_3.Pin_0, 4040_2.Input_signal
  N36: LM324.1IN-, Jamp5.pin1
  N37: LM324.1IN+, 100K_3.Pin_1, 1K_3.Pin_0
  N38: LM324.2IN+, 100K_2.Pin_0, 1K_2.Pin_1
  N39: LM324.2IN-, Jamp4.pin1
  N40: LM324.3OUT, 100K.Pin_0, 4_7k4.Pin_1
  N41: LM324.3IN-, Jamp1.pin1
  N42: LM324.3IN+, 100K.Pin_1, 1K.Pin_1
  N43: 1K.Pin_0, Jamp2.pin1, Jamp2.pin2
  N44: 1K_2.Pin_0, Jamp3.pin2
  N45: 1K_3.Pin_1, Jamp6.pin1, Jamp6.pin2
  N46: 4040_2.Q13, j41.pin1
  N47: 4040_2.Q14, j41.pin2
  N48: 4040_2.Q6, j41.pin3
  N49: 4040_2.Q5, j41.pin4
  N50: 4040_2.Q7, j41.pin5
  N51: 4040_2.Q4, j41.pin6
  N52: opcom.pin1, opcom.pin2
  N53: LED3.anode, 100_2.Pin_1
  N54: 100_3.Pin_0, LED4.anode

notes:
  moat
  blueprint@poetaster.de 2024

custom parts:
  CD4040E: CD4020B, CD4024B, and CD4040B are ripple-carry binary counters. All counter stages are master-slave flip-flops. The state of a counter advances one count on the negative transition of each input pulse; a high level on the RESET line resets the counter to its all zeros state. Schmitt trigger action on the input-pulse line permits unlimited rise and fall times. All inputs and outputs are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
