# Fritzing sketch moat.v2 (saved by Fritzing 0.9.3b)
circuit board: 8.4cm x 5.5cm
breadboards: 1

parts:
  100Klfo = Rotary Potentiometer (Small) [maximum_resistance=100kΩ package=THT]
  100Km2 = Rotary Potentiometer (Small) [maximum_resistance=100kΩ package=THT]
  100Kx2 = Rotary Potentiometer (Small) [maximum_resistance=100kΩ package=THT]
  100Kmx = Rotary Potentiometer (Small) [maximum_resistance=100kΩ package=THT]
  4040 = CD4040E [package="DIP16 [THT]"]
  XR = XR2206 [package=dil16]
  100Kosc = Rotary Potentiometer (Small) [maximum_resistance=100kΩ package=THT]
  100Kx1 = Rotary Potentiometer (Small) [maximum_resistance=100kΩ package=THT]
  1uf = Electrolytic Capacitor [capacitance=1µF voltage=16V package="100 mil [THT, electrolytic]"]
  100Km1 = Rotary Potentiometer (Small) [maximum_resistance=100kΩ package=THT]
  Jm1 = female pin header, 3 pins [form="♀ (female)"]
  Jm2 = female pin header, 3 pins [form="♀ (female)"]
  40106 = IC, DIP package, 14 pins [chip_label=40106 spacing=300mil]
  47nf = Ceramic Capacitor [capacitance=47nF voltage=16V package="200 mil [THT, multilayer]"]
  LED2 = LED - 3mm [color="White (8000K)" package="3 mm [THT]"]
  j40 = female pin header, 6 pins [form="♀ (female)"]
  Jp- = female pin header, 2 pins [form="♀ (female)"]
  Jp+ = female pin header, 2 pins [form="♀ (female)"]
  4_7k = Resistor [tolerance=±5% resistance=4.7k package=THT]
  Jx1 = female pin header, 2 pins [form="♀ (female)"]
  Jxs = female pin header, 2 pins [form="♀ (female)"]
  Jxa = female pin header, 2 pins [form="♀ (female)"]
  Jxo = female pin header, 2 pins [form="♀ (female)"]
  R17 = Resistor [tolerance=±5% resistance=4.7k package=THT]
  10uf = Electrolytic Capacitor [capacitance=10µF voltage=16V package="100 mil [THT, electrolytic]"]
  10uf_2 = Electrolytic Capacitor [capacitance=10μF voltage=16V package="100 mil [THT, electrolytic]"]
  R14 = Resistor [tolerance=±5% resistance=10k package=THT]
  R13 = Resistor [tolerance=±5% resistance=10k package=THT]
  Jx2 = female pin header, 2 pins [form="♀ (female)"]
  1uf_2 = Electrolytic Capacitor [capacitance=1µF voltage=16V package="100 mil [THT, electrolytic]"]
  4_7k_2 = Resistor [tolerance=±5% resistance=4.7k package=THT]
  47nf_2 = Ceramic Capacitor [capacitance=47nF voltage=16V package="200 mil [THT, multilayer]"]
  R18 = Resistor [tolerance=±5% resistance=330 package=THT]
  LED3 = LED - 3mm [color="White (8000K)" package="3 mm [THT]"]
  jlfo = female pin header, 2 pins [form="♀ (female)"]
  LDR = Photocell (LDR) [package=THT]
  20K = Trimmer Potentiometer [maximum_resistance=20kΩ package=THT]
  5k = Resistor [tolerance=±1% resistance=1k package=THT]
  5k_2 = Resistor [tolerance=±1% resistance=1k package=THT]
  20K_2 = Trimmer Potentiometer [maximum_resistance=20kΩ package=THT]
  10Kflt = Rotary Potentiometer (Small) [maximum_resistance=10kΩ package=THT]
  1uf_3 = Electrolytic Capacitor [capacitance=1µF voltage=16V package="100 mil [THT, electrolytic]"]
  Jmix = female pin header, 2 pins [form="♀ (female)"]
  Josc = female pin header, 2 pins [form="♀ (female)"]
  Josc_2 = female pin header, 2 pins [form="♀ (female)"]
  j40_2 = female pin header, 2 pins [form="♀ (female)"]
  j40in = female pin header, 2 pins [form="♀ (female)"]
  Jled = female pin header, 2 pins [form="♀ (female)"]
  R19 = Resistor [tolerance=±5% resistance=220 package=THT]

nets:
  N1: 100Klfo.wiper, 40106.pin5, 10uf_2.+
  N2: 100Klfo.leg2, 4040.Input_signal, 40106.pin6, R18.Pin_0, j40in.pin1, j40in.pin2
  VSS: 100Km2.leg1, 100Km2.wiper, 100Km2.leg2, 100Kx2.leg2, 100Kmx.wiper, 4040.Q14, 4040.Q6, 4040.Q5, 4040.Q7, 4040.Q4, 4040.Vss, XR.GND, 100Kx1.leg2, 1uf.-, 100Km1.leg1, 100Km1.leg2, Jm1.pin1, Jm1.pin3, Jm2.pin1, Jm2.pin2, Jm2.pin3, 40106.pin7, 47nf.1, LED2.cathode, LED2.anode, j40.pin2, j40.pin3, j40.pin4, j40.pin5, j40.pin6, Jp-.pin1, Jp-.pin2, 10uf.-, 10uf_2.-, LED3.cathode, LDR.pin_1, 20K.wiper, 5k_2.Pin_0, 10Kflt.wiper, 1uf_3.-, Jmix.pin1, Jmix.pin2
  N3: 100Kx2.leg1, Jx2.pin1, Jx2.pin2
  N4: 100Kx2.wiper, 4_7k.Pin_1
  N5: 100Kmx.leg1, 47nf.0, 10Kflt.leg2
  N6: 100Kmx.leg2, Jxo.pin1, Jxo.pin2, 1uf_2.+
  N7: 4040.Q13, 100Km1.wiper, Jm1.pin2, j40.pin1, LED3.anode, Jled.pin1, Jled.pin2
  N8: 4040.Q1, j40_2.pin1, j40_2.pin2
  VDD: 4040.Vdd, XR.VCC, 40106.pin14, Jp+.pin1, Jp+.pin2, R17.Pin_0, 5k.Pin_0
  N9: XR.AMSI, Jxa.pin1, Jxa.pin2
  N10: XR.STO, 1uf_2.-
  N11: XR.MO, 20K_2.leg2
  N12: XR.TC1, 47nf_2.0
  N13: XR.TC2, 47nf_2.1
  N14: XR.TR1, 4_7k_2.Pin_0
  N15: XR.TR2, 4_7k.Pin_0
  N16: XR.FSKI, Jxs.pin1, Jxs.pin2
  N17: XR.BIAS, 10uf.+
  N18: XR.SYNCO, R17.Pin_1
  N19: XR.WAVEA1, R19.Pin_1
  N20: XR.WAVEA2, R19.Pin_0
  N21: XR.SYMA1, 20K.leg2
  N22: XR.SYMA2, 20K.leg1
  N23: 100Kosc.wiper, 1uf.+, 40106.pin9, R14.Pin_0, R13.Pin_0
  N24: 100Kosc.leg2, 40106.pin8, LDR.pin_0
  N25: 100Kx1.leg1, Jx1.pin1, Jx1.pin2
  N26: 100Kx1.wiper, 4_7k_2.Pin_1
  N27: R14.Pin_1, Josc.pin1, Josc.pin2
  N28: R13.Pin_1, Josc_2.pin1, Josc_2.pin2
  N29: R18.Pin_1, jlfo.pin1, jlfo.pin2
  N30: 5k.Pin_1, 5k_2.Pin_1, 20K_2.leg1, 20K_2.wiper
  N31: 10Kflt.leg1, 1uf_3.+

custom parts:
  CD4040E: CD4020B, CD4024B, and CD4040B are ripple-carry binary counters. All counter stages are master-slave flip-flops. The state of a counter advances one count on the negative transition of each input pulse; a high level on the RESET line resets the counter to its all zeros state. Schmitt trigger action on the input-pulse line permits unlimited rise and fall times. All inputs and outputs are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
